// Logisim project ESF.circ as structural Verilog: 19 circuits, main circuit main
module main (
  output halt,
  output [31:0] out_2,
  output [31:0] out_3
);

  wire and_1_out, and_2_out, clock_1_out, counter_1_carry, decoder_1_out1, decoder_1_out2, decoder_1_out3,
       decoder_1_out4, decoder_1_out5, multiplexer_1_out, multiplexer_9_out, or_1_out;
  wire [2:0] counter_1_q;
  wire [4:0] adder_1_out, counter_2_q;
  wire [15:0] key_schedule_1_out_5, multiplexer_6_out, register_6_q;
  wire [31:0] extract_key_1_out_4, key_schedule_1_out_6, key_schedule_1_out_7, left_shift_by_7_bits_1_out_2,
       multiplexer_2_out, multiplexer_3_out, multiplexer_7_out, multiplexer_8_out, ram_1_data, register_1_q,
       register_2_q, register_3_q, register_4_q, register_5_q, register_7_q, register_8_q, register_9_q,
       register_10_q, round_function_1_out_3, xor_1_out;

  Clock clock_1 (.out(clock_1_out));
  Multiplexer multiplexer_1 (
    .in0(clock_1_out), .in1(1'b1), .out(multiplexer_1_out), .sel(counter_1_carry));  // open: en
  Counter #(.width(3), .max('h6)) counter_1 (
    .Q(counter_1_q), .carry(counter_1_carry), .clk(multiplexer_1_out));  // open: load, D, count, clr
  RAM #(.addrWidth(3), .dataWidth(32)) ram_1 (.addr(counter_1_q), .data(ram_1_data));  // open: sel, clk, ld, clr
  and and_1 (and_1_out, clock_1_out, counter_1_carry);
  Register #(.width(32)) register_1 (.D(xor_1_out), .Q(register_1_q), .clk(multiplexer_9_out));  // open: en, clr
  Decoder #(.select(3)) decoder_1 (
    .out1(decoder_1_out1), .out2(decoder_1_out2), .out3(decoder_1_out3), .out4(decoder_1_out4),
    .out5(decoder_1_out5), .sel(counter_1_q));  // open: out0, out6, out7, en
  Register #(.width(32)) register_2 (
    .D(multiplexer_3_out), .Q(register_2_q), .clk(multiplexer_9_out));  // open: en, clr
  Multiplexer #(.width(32), .enable("false")) multiplexer_2 (
    .in0(register_3_q), .in1(register_2_q), .out(multiplexer_2_out), .sel(or_1_out));
  Left_Shift_by_7_bits left_shift_by_7_bits_1 (.in_1(multiplexer_2_out), .out_2(left_shift_by_7_bits_1_out_2));
  Register #(.width(32)) register_3 (.D(ram_1_data), .Q(register_3_q), .clk(decoder_1_out2));  // open: en, clr
  Register #(.width(32)) register_4 (.D(ram_1_data), .Q(register_4_q), .clk(decoder_1_out1));  // open: en, clr
  Multiplexer #(.width(32), .enable("false")) multiplexer_3 (
    .in0(register_4_q), .in1(register_1_q), .out(multiplexer_3_out), .sel(or_1_out));
  Round_Function round_function_1 (
    .in_1(extract_key_1_out_4), .in_2(multiplexer_3_out), .out_3(round_function_1_out_3));
  assign xor_1_out = left_shift_by_7_bits_1_out_2 ^ round_function_1_out_3;  // XOR_Gate xor_1, 32 bits wide
  Multiplexer #(.width(32), .enable("false")) multiplexer_4 (.in1(xor_1_out), .out(out_2), .sel(halt));  // open: in0
  Register #(.width(32)) register_5 (.D(ram_1_data), .Q(register_5_q), .clk(decoder_1_out5));  // open: en, clr
  Register #(.width(16)) register_6 (
    .D(key_schedule_1_out_5), .Q(register_6_q), .clk(multiplexer_9_out));  // open: en, clr
  Multiplexer #(.width(32), .enable("false")) multiplexer_5 (
    .in1(multiplexer_3_out), .out(out_3), .sel(halt));  // open: in0
  Register #(.width(32)) register_7 (.D(ram_1_data), .Q(register_7_q), .clk(decoder_1_out4));  // open: en, clr
  Multiplexer #(.width(16), .enable("false")) multiplexer_6 (
    .in0(register_5_q[15:0]), .in1(register_6_q), .out(multiplexer_6_out), .sel(or_1_out));
  Extract_Key extract_key_1 (
    .out_4(extract_key_1_out_4), .in_1(multiplexer_6_out), .in_2(multiplexer_7_out), .in_3(multiplexer_8_out));
  Multiplexer #(.width(32), .enable("false")) multiplexer_7 (
    .in0(register_7_q), .in1(register_8_q), .out(multiplexer_7_out), .sel(or_1_out));
  Register #(.width(32)) register_8 (
    .D(key_schedule_1_out_6), .Q(register_8_q), .clk(multiplexer_9_out));  // open: en, clr
  Key_Schedule key_schedule_1 (
    .in_1(multiplexer_6_out), .in_2(multiplexer_7_out), .in_3(multiplexer_8_out),
    .out_5(key_schedule_1_out_5), .out_6(key_schedule_1_out_6), .out_7(key_schedule_1_out_7),
    .Round_Clock(adder_1_out));
  Register #(.width(32)) register_9 (.D(ram_1_data), .Q(register_9_q), .clk(decoder_1_out3));  // open: en, clr
  Multiplexer #(.width(32), .enable("false")) multiplexer_8 (
    .in0(register_9_q), .in1(register_10_q), .out(multiplexer_8_out), .sel(or_1_out));
  Adder #(.width(5)) adder_1 (.a(5'b00001), .b(counter_2_q), .out(adder_1_out));  // open: cin, cout
  Register #(.width(32)) register_10 (
    .D(key_schedule_1_out_7), .Q(register_10_q), .clk(multiplexer_9_out));  // open: en, clr
  Counter #(.width(5), .max('h1f), .ongoal("stay")) counter_2 (
    .Q(counter_2_q), .carry(halt), .clk(multiplexer_9_out));  // open: load, D, count, clr
  Multiplexer #(.enable("false")) multiplexer_9 (.in0(and_1_out), .in1(1'b1), .out(multiplexer_9_out), .sel(and_2_out));
  or or_1 (or_1_out, counter_2_q[0], counter_2_q[1], counter_2_q[2], counter_2_q[3], counter_2_q[4]);
  and and_2 (and_2_out, counter_2_q[0], counter_2_q[1], counter_2_q[2], counter_2_q[3], counter_2_q[4]);
endmodule

module S_box_0 (
  input  [3:0] in_1,
  output [3:0] out_2
);

  Multiplexer #(.select(4), .width(4), .enable("false")) multiplexer_1 (
    .in0(4'b0011), .in1(4'b1000), .in2(4'b1111), .in3(4'b0001), .in4(4'b1010), .in5(4'b0110), .in6(4'b0101),
    .in7(4'b1011), .in8(4'b1110), .in9(4'b1101), .in10(4'b0100), .in11(4'b0010), .in12(4'b0111),
    .in13(4'b0000), .in14(4'b1001), .in15(4'b1100), .out(out_2), .sel(in_1));
endmodule

module S_box_1 (
  input  [3:0] in_1,
  output [3:0] out_2
);

  Multiplexer #(.select(4), .width(4), .enable("false")) multiplexer_1 (
    .in0(4'b1111), .in1(4'b1100), .in2(4'b0010), .in3(4'b0111), .in4(4'b1001), .in5(4'b0000), .in6(4'b0101),
    .in7(4'b1010), .in8(4'b0001), .in9(4'b1011), .in10(4'b1110), .in11(4'b1000), .in12(4'b0110),
    .in13(4'b1101), .in14(4'b0011), .in15(4'b0100), .out(out_2), .sel(in_1));
endmodule

module S_box_2 (
  input  [3:0] in_1,
  output [3:0] out_2
);

  Multiplexer #(.select(4), .width(4), .enable("false")) multiplexer_1 (
    .in0(4'b1000), .in1(4'b0110), .in2(4'b0111), .in3(4'b1001), .in4(4'b0011), .in5(4'b1100), .in6(4'b1010),
    .in7(4'b1111), .in8(4'b1101), .in9(4'b0001), .in10(4'b1110), .in11(4'b0100), .in12(4'b0000),
    .in13(4'b1011), .in14(4'b0101), .in15(4'b0010), .out(out_2), .sel(in_1));
endmodule

module S_box_3 (
  input  [3:0] in_1,
  output [3:0] out_2
);

  Multiplexer #(.select(4), .width(4), .enable("false")) multiplexer_1 (
    .in0(4'b0000), .in1(4'b1111), .in2(4'b1011), .in3(4'b1000), .in4(4'b1100), .in5(4'b1001), .in6(4'b0110),
    .in7(4'b0011), .in8(4'b1101), .in9(4'b0001), .in10(4'b0010), .in11(4'b0100), .in12(4'b1010),
    .in13(4'b0111), .in14(4'b0101), .in15(4'b1110), .out(out_2), .sel(in_1));
endmodule

module S_box_4 (
  input  [3:0] in_1,
  output [3:0] out_2
);

  Multiplexer #(.select(4), .width(4), .enable("false")) multiplexer_1 (
    .in0(4'b0001), .in1(4'b1111), .in2(4'b1000), .in3(4'b0011), .in4(4'b1100), .in5(4'b0000), .in6(4'b1011),
    .in7(4'b0110), .in8(4'b0010), .in9(4'b0101), .in10(4'b0100), .in11(4'b1010), .in12(4'b1001),
    .in13(4'b1110), .in14(4'b0111), .in15(4'b1101), .out(out_2), .sel(in_1));
endmodule

module S_box_5 (
  input  [3:0] in_1,
  output [3:0] out_2
);

  Multiplexer #(.select(4), .width(4), .enable("false")) multiplexer_1 (
    .in0(4'b1111), .in1(4'b0101), .in2(4'b0010), .in3(4'b1011), .in4(4'b0100), .in5(4'b1010), .in6(4'b1001),
    .in7(4'b1100), .in8(4'b0000), .in9(4'b0011), .in10(4'b1110), .in11(4'b1000), .in12(4'b1101),
    .in13(4'b0110), .in14(4'b0111), .in15(4'b0001), .out(out_2), .sel(in_1));
endmodule

module S_box_6 (
  input  [3:0] in_1,
  output [3:0] out_2
);

  Multiplexer #(.select(4), .width(4), .enable("false")) multiplexer_1 (
    .in0(4'b0111), .in1(4'b0010), .in2(4'b1100), .in3(4'b0101), .in4(4'b1000), .in5(4'b0100), .in6(4'b0110),
    .in7(4'b1011), .in8(4'b1110), .in9(4'b1001), .in10(4'b0001), .in11(4'b1111), .in12(4'b1101),
    .in13(4'b0011), .in14(4'b1010), .in15(4'b0000), .out(out_2), .sel(in_1));
endmodule

module S_box_7 (
  input  [3:0] in_1,
  output [3:0] out_2
);

  Multiplexer #(.select(4), .width(4), .enable("false")) multiplexer_1 (
    .in0(4'b0001), .in1(4'b1101), .in2(4'b1111), .in3(4'b0000), .in4(4'b1110), .in5(4'b1000), .in6(4'b0010),
    .in7(4'b1011), .in8(4'b0111), .in9(4'b0100), .in10(4'b1100), .in11(4'b1010), .in12(4'b1001),
    .in13(4'b0011), .in14(4'b0101), .in15(4'b0110), .out(out_2), .sel(in_1));
endmodule

module S_box_layer (
  input  [31:0] in_1,
  output [31:0] out_2
);

  S_box_6 s_box_6_1 (.in_1(in_1[27:24]), .out_2(out_2[27:24]));
  S_box_7 s_box_7_1 (.in_1(in_1[31:28]), .out_2(out_2[31:28]));
  S_box_4 s_box_4_1 (.in_1(in_1[19:16]), .out_2(out_2[19:16]));
  S_box_5 s_box_5_1 (.in_1(in_1[23:20]), .out_2(out_2[23:20]));
  S_box_2 s_box_2_1 (.in_1(in_1[11:8]), .out_2(out_2[11:8]));
  S_box_3 s_box_3_1 (.in_1(in_1[15:12]), .out_2(out_2[15:12]));
  S_box_0 s_box_0_1 (.in_1(in_1[3:0]), .out_2(out_2[3:0]));
  S_box_1 s_box_1_1 (.in_1(in_1[7:4]), .out_2(out_2[7:4]));
endmodule

module P_box_16_bit (
  input  [15:0] in_1,
  output [3:0] out_2,
  output [3:0] out_3,
  output [3:0] out_4,
  output [3:0] out_5
);

  P_box_4_bit p_box_4_bit_1 (
    .in_1(in_1[15:12]), .out_2(out_2[3]), .out_3(out_3[3]), .out_4(out_4[3]), .out_5(out_5[3]));
  P_box_4_bit p_box_4_bit_2 (.in_1(in_1[11:8]), .out_2(out_2[2]), .out_3(out_3[2]), .out_4(out_4[2]), .out_5(out_5[2]));
  P_box_4_bit p_box_4_bit_3 (.in_1(in_1[7:4]), .out_2(out_2[1]), .out_3(out_3[1]), .out_4(out_4[1]), .out_5(out_5[1]));
  P_box_4_bit p_box_4_bit_4 (.in_1(in_1[3:0]), .out_2(out_2[0]), .out_3(out_3[0]), .out_4(out_4[0]), .out_5(out_5[0]));
endmodule

module P_box_4_bit (
  input  [3:0] in_1,
  output out_2,
  output out_3,
  output out_4,
  output out_5
);


  assign out_2 = in_1[3];
  assign out_3 = in_1[2];
  assign out_4 = in_1[1];
  assign out_5 = in_1[0];
endmodule

module P_box_layer (
  input  [31:0] in_1,
  output [31:0] out_2
);

  P_box_16_bit p_box_16_bit_1 (
    .in_1(in_1[31:16]), .out_2(out_2[31:28]), .out_3(out_2[23:20]), .out_4(out_2[15:12]), .out_5(out_2[7:4]));
  P_box_16_bit p_box_16_bit_2 (
    .in_1(in_1[15:0]), .out_2(out_2[27:24]), .out_3(out_2[19:16]), .out_4(out_2[11:8]), .out_5(out_2[3:0]));
endmodule

module Round_Function (
  input  [31:0] in_1,
  input  [31:0] in_2,
  output [31:0] out_3
);

  wire [31:0] s_box_layer_1_out_2, xor_1_out;

  assign xor_1_out = in_1 ^ in_2;  // XOR_Gate xor_1, 32 bits wide
  S_box_layer s_box_layer_1 (.in_1(xor_1_out), .out_2(s_box_layer_1_out_2));
  P_box_layer p_box_layer_1 (.in_1(s_box_layer_1_out_2), .out_2(out_3));
endmodule

module Left_Shift_by_7_bits (
  input  [31:0] in_1,
  output [31:0] out_2
);


  assign out_2 = {in_1[24:0], in_1[31:25]};
endmodule

module Key_Schedule (
  input  [15:0] in_1,
  input  [31:0] in_2,
  input  [31:0] in_3,
  input  [4:0] Round_Clock,
  output [15:0] out_5,
  output [31:0] out_6,
  output [31:0] out_7
);

  wire [15:0] left_shift_by_13_bits_1_out_6;
  wire [31:0] left_shift_by_13_bits_1_out_4, left_shift_by_13_bits_1_out_5;

  Left_Shift_by_13_bits left_shift_by_13_bits_1 (
    .in_1(in_1), .in_2(in_2), .in_3(in_3), .out_6(left_shift_by_13_bits_1_out_6),
    .out_4(left_shift_by_13_bits_1_out_4), .out_5(left_shift_by_13_bits_1_out_5));
  Pass_via_S_box_and_XOR_with_Round_Clock pass_via_s_box_and_xor_with_round_clock_1 (
    .in_1(left_shift_by_13_bits_1_out_6), .in_2(left_shift_by_13_bits_1_out_4),
    .in_3(left_shift_by_13_bits_1_out_5), .out_7(out_5), .out_5(out_6), .out_6(out_7), .in_4(Round_Clock));
endmodule

module Left_Shift_by_13_bits (
  input  [15:0] in_1,
  input  [31:0] in_2,
  input  [31:0] in_3,
  output [31:0] out_4,
  output [31:0] out_5,
  output [15:0] out_6
);


  assign out_4 = {in_2[18:0], in_3[31:19]};
  assign out_5 = {in_3[18:0], in_1[15:3]};
  assign out_6 = {in_1[2:0], in_2[31:19]};
endmodule

module Pass_via_S_box_and_XOR_with_Round_Clock (
  input  [15:0] in_1,
  input  [31:0] in_2,
  input  [31:0] in_3,
  input  [4:0] in_4,
  output [31:0] out_5,
  output [31:0] out_6,
  output [15:0] out_7
);

  S_box_0 s_box_0_1 (.in_1(in_1[15:12]), .out_2(out_7[15:12]));
  S_box_0 s_box_0_2 (.in_1(in_1[11:8]), .out_2(out_7[11:8]));
  assign out_5[15:11] = in_2[15:11] ^ in_4;  // XOR_Gate xor_1, 5 bits wide

  assign {out_5[31:16], out_5[10:0]} = {in_2[31:16], in_2[10:0]};
  assign out_6 = in_3;
  assign out_7[7:0] = in_1[7:0];
endmodule

module Extract_Key (
  input  [15:0] in_1,
  input  [31:0] in_2,
  input  [31:0] in_3,
  output [31:0] out_4
);


  assign out_4 = {in_1, in_2[31:16]};
endmodule
